# Fritzing sketch Circuit design (saved by Fritzing 0.9.3b)
circuit board: 8.46667cm x 5.64444cm
breadboards: 1

parts:
  Part1 = Arduino Uno (Rev3) - ICSP
  R1 = Resistor [tolerance=±5% resistance=100k package="2512 [SMD]"]
  R2 = Resistor [tolerance=±5% resistance=20k package="2512 [SMD]"]

nets:
  N1: Part1.A0, R1.Pin_1, R2.Pin_0
  N2: Part1.5V, R1.Pin_0
  N3: Part1.GND, R2.Pin_1

notes:
  Arduono DC Meter
  Voltage Divider
  Input <= 30V.
  Output => 5V.
  R1 => 100K
  R2 => 20K
